# Fritzing sketch Untitled Sketch 2 (saved by Fritzing 0.9.3b)
breadboards: 1

parts:
  Part1 = Arduino Uno (Rev3)
  LED1 = LED - 5mm [color="Red (633nm)" package="5 mm [THT]"]
  LED2 = LED - 5mm [color="Red (633nm)" package="5 mm [THT]"]
  R1 = Resistor [tolerance=±5% resistance=220 package=THT]
  R2 = Resistor [tolerance=±5% resistance=220 package=THT]
  Matrix_keypad1 = KEYPAD 4x4

nets:
  N1: Part1.D8, Matrix_keypad1.col2
  N2: Part1.D9_PWM, Matrix_keypad1.col1
  N3: Part1.D11_PWM/MOSI, R1.Pin_0
  N4: Part1.D2, Matrix_keypad1.row1
  N5: Part1.D3_PWM, Matrix_keypad1.row2
  N6: Part1.D4, Matrix_keypad1.row3
  N7: Part1.D5_PWM, Matrix_keypad1.row4
  N8: Part1.D6_PWM, Matrix_keypad1.col4
  N9: Part1.D7, Matrix_keypad1.col3
  N10: Part1.GND, LED1.cathode, LED2.cathode
  N11: LED1.anode, R1.Pin_1
  N12: LED2.anode, R2.Pin_1

custom parts:
  KEYPAD 4x4: Matrix keypad 16 buttons, 4 rows x 4 columns
